# Fritzing sketch arduino-uno-tilt-switch-5050-controller-shield (saved by Fritzing 0.8.5b)
breadboards: 1

parts:
  Part1 = Arduino Uno (Rev3)
  Q2 = MOSFET-NCHANNEL [package=to220v]
  Q3 = MOSFET-NCHANNEL [package=to220v]
  R2 = Resistor [tolerance=±5% resistance=12k package=THT]
  Q4 = MOSFET-NCHANNEL [package=to220v]
  R3 = Resistor [tolerance=±5% resistance=12k package=THT]
  LED_Strip = RGB LED (com. anode, rbg) [package="5 mm [THT]"]
  R1 = Resistor [tolerance=±5% resistance=12k package=THT]
  S1 = Tilt Switch [package=THT]
  R4 = Resistor [tolerance=±5% resistance=12k package=THT]
  R5 = Resistor [tolerance=±5% resistance=12k package=THT]
  S2 = Tilt Switch [package=THT]
  R6 = Resistor [tolerance=±5% resistance=12k package=THT]
  S3 = Tilt Switch [package=THT]

nets:
  N1: Part1.D9_PWM, Q4.G, R3.Pin_0
  N2: Part1.D10_PWM/SS, Q3.G, R2.Pin_0
  N3: Part1.D11_PWM/MOSI, Q2.G, R1.Pin_0
  N4: Part1.GND, Q2.S, Q3.S, R2.Pin_1, Q4.S, R3.Pin_1, R1.Pin_1, R4.Pin_1, R5.Pin_1, R6.Pin_1
  N5: Part1.D2, R6.Pin_0, S3.Pin_1
  N6: Part1.D3_PWM, R5.Pin_0, S2.Pin_1
  N7: Part1.D4, S1.Pin_1, R4.Pin_0
  N8: Part1.5V, S1.Pin_2, S2.Pin_2, S3.Pin_2
  N9: Q2.D, LED_Strip.red_cathode
  N10: Q3.D, LED_Strip.blue_cathode
  N11: Q4.D, LED_Strip.green_cathode

notes:
  Tilt switches should be angled into an approximate pyramid to detect a 90 degree tilt in any of four directions
  Standard 5V power supply to Arduino
  is attached to either port
  Note that (-) terminals are joined between 12V and 5V supplies, but the (+) terminals are not.
  Standard 12V power supply for LED strips attached here
